// Logisim project instruction-set-architecture.circ as structural Verilog: 4 circuits, main circuit main
module main (
  output [7:0] out_1,
  output [7:0] out_2,
  output [7:0] out_3,
  output [3:0] out_4,
  output [15:0] out_5,
  output [1:0] Register_2,
  output [1:0] Register_1,
  output [7:0] out_8,
  output [7:0] out_9,
  output [7:0] Adder,
  output [7:0] out_11,
  output [7:0] out_12
);

  wire Add, clock_1_out, Halt, Load, not_1_out, R1_Enable, R1_Enable_Add, R1_Enable_Load, R2_Enable,
       R2_Enable_Add, R2_Enable_Load, reg_decoder_1_r1, reg_decoder_1_r2, reg_decoder_2_r1, reg_decoder_2_r2,
       Write;

  PC PC (.Program_Counter(out_8));
  Register R3 (.D(out_11), .en(Add), .Q(out_1), .clk(clock_1_out));  // open: clr
  Register R1 (.D(out_5[7:0]), .en(R1_Enable), .Q(out_2), .clk(clock_1_out));  // open: clr
  Register R2 (.D(out_5[7:0]), .en(R2_Enable), .Q(out_3), .clk(clock_1_out));  // open: clr
  Multiplexer #(.select(2), .width(8)) multiplexer_1 (
    .in1(out_2), .in2(out_3), .out(Adder), .sel(out_5[11:10]));  // open: in0, in3, en
  Multiplexer #(.select(2), .width(8)) multiplexer_2 (
    .in1(out_2), .in2(out_3), .out(out_12), .sel(out_5[9:8]));  // open: in0, in3, en
  not not_1 (not_1_out, Halt);
  ROM #(.dataWidth(16)) rom_1 (.addr(out_8), .data({out_4, out_5[11:0]}), .sel(not_1_out));
  Adder adder_1 (.a(Adder), .b(out_12), .out(out_11));  // open: cin, cout
  OP_Code_Decoder op_code_decoder_1 (
    .a0(out_4[3]), .in_2(out_4[2]), .in_3(out_4[1]), .a4(out_4[0]), .Halt(Halt), .Add(Add), .Write(Write),
    .Load(Load));
  Reg_Decoder reg_decoder_1 (.a0(out_5[10]), .a1(out_5[11]), .R2(reg_decoder_1_r2), .R1(reg_decoder_1_r1));
  Reg_Decoder reg_decoder_2 (.a0(out_5[10]), .a1(out_5[11]), .R2(reg_decoder_2_r2), .R1(reg_decoder_2_r1));
  Clock clock_1 (.out(clock_1_out));
  RAM #(.bus("separate")) ram_1 (
    .addr(out_5[7:0]), .din(out_1), .str(Write), .clk(clock_1_out));  // open: data, sel, ld, clr
  and and_1 (R1_Enable_Add, Add, reg_decoder_1_r1);
  and and_2 (R2_Enable_Add, Add, reg_decoder_1_r2);
  or or_1 (R1_Enable, R1_Enable_Load, R1_Enable_Add);
  or or_2 (R2_Enable, R2_Enable_Load, R2_Enable_Add);
  and and_3 (R1_Enable_Load, Load, reg_decoder_2_r1);
  and and_4 (R2_Enable_Load, Load, reg_decoder_2_r2);

  assign out_5[15:12] = out_4;
  assign out_9 = out_5[7:0];
  assign Register_1 = out_5[11:10];
  assign Register_2 = out_5[9:8];

  // Other names for the same wires on the sheet: Address[7:0] = out_5[7:0]; Data[7:0] = out_5[7:0];
  //   R1_In[7:0] = out_5[7:0]; R2_In[7:0] = out_5[7:0]; R1_Out[7:0] = out_2; R2_Out[7:0] = out_3; R3_Enable = Add;
  //   R3_In[7:0] = out_11; R3_Out[7:0] = out_1

  // Notes on the sheet:
  //   Value from Register 2
  //   Registers
  //   ROM
  //   contents of rom_1 (hex, n*v repeats v):
  //   401 802 2600 1401 403 804 2600 1402 405 806 2600 1403 407 808 2600 1404 409 80a 2600 1405 40b 80c
  //   2600 1406 40d 80e 2600 1407 40f 810 2600 1408 411 812 2600 1409
  //   Write
  //   Add
  //   Load
endmodule

module OP_Code_Decoder (
  input  a0,
  input  in_2,
  input  in_3,
  input  a4,
  output Halt,
  output Add,
  output Write,
  output Load
);

  wire not_1_out, not_2_out, not_3_out, not_4_out;

  not not_1 (not_1_out, a0);
  not not_2 (not_2_out, in_2);
  not not_3 (not_3_out, in_3);
  not not_4 (not_4_out, a4);
  and and_1 (Halt, not_1_out, not_2_out, in_3, a4);
  and and_2 (Add, not_1_out, not_2_out, in_3, not_4_out);
  and and_3 (Write, not_1_out, not_2_out, not_3_out, a4);
  and and_4 (Load, not_1_out, not_2_out, not_3_out, not_4_out);
endmodule

module Reg_Decoder (
  input  a0,
  input  a1,
  output R2,
  output R1
);

  wire and_1_out, and_4_out, not_1_out, not_2_out;

  not not_1 (not_1_out, a1);
  not not_2 (not_2_out, a0);
  and and_1 (and_1_out, a0, a1);
  and and_2 (R2, not_2_out, a1);
  and and_3 (R1, a0, not_1_out);
  and and_4 (and_4_out, not_2_out, not_1_out);

  // Notes on the sheet:
  //   No Register
  //   No Register
endmodule

module PC (
  output [7:0] Program_Counter
);

  wire clock_1_out, Reset_out;
  wire [7:0] adder_1_out;

  Clock clock_1 (.out(clock_1_out));
  Register register_1 (.D(adder_1_out), .Q(Program_Counter), .clk(clock_1_out), .clr(Reset_out));  // open: en
  Button Reset (.out(Reset_out));
  Adder adder_1 (.a(Program_Counter), .b(8'h1), .out(adder_1_out));  // open: cin, cout

  // Notes on the sheet:
  //   Program Counter
endmodule
